# Fritzing sketch ElectroMagPCB (saved by Fritzing 0.9.3b)
circuit board: 4.84971cm x 5.72386cm
breadboards: 1

parts:
  J1 = female pin header, 17 pins [form="♀ (female)"]
  J2 = female pin header, 17 pins [form="♀ (female)"]
  J3 = Screw terminal - 2 pins [package=THT]
  J4 = female pin header, 3 pins [form="♀ (female)"]
  J5 = Screw terminal - 2 pins [package=THT]
  D1 = Rectifier Diode [part_number=1N4001 package="300 mil [THT]"]
  J6 = female pin header, 3 pins [form="♀ (female)"]
  J7 = female pin header, 2 pins [form="♀ (female)"]
  J8 = female pin header, 2 pins [form="♀ (female)"]
  J9 = female pin header, 3 pins [form="♀ (female)"]
  J10 = female pin header, 2 pins [form="♀ (female)"]
  R1 = Resistor [tolerance=±5% resistance=220 package=THT]
  R2 = Resistor [tolerance=±5% resistance=220 package=THT]

nets:
  N1: J1.pin10, J9.pin3
  N2: J1.pin12, J9.pin1
  N3: J1.pin14, J3.pin1, J4.pin2, J6.pin3
  N4: J1.pin15, J3.pin2, J4.pin3, J7.pin2
  N5: J2.pin1, R1.Pin_0
  N6: J2.pin3, R2.Pin_0
  N7: J2.pin12, J9.pin2, J10.pin1
  N8: J4.pin1, J5.pin2, D1.anode, J8.pin1
  N9: J5.pin1, D1.cathode, J6.pin2
  N10: J6.pin1, R2.Pin_1
  N11: J10.pin2, R1.Pin_1

notes:
  +
